# Fritzing sketch SensorBoard (saved by Fritzing 0.9.3b)
breadboards: 1

parts:
  R1 = Resistor [tolerance=±5% resistance=5k package=THT]
  R2 = Resistor [tolerance=±5% resistance=5k package=THT]
  U1 = LM358 [package=dip08]
  V2-in = female pin header, 2 pins [form="♀ (female)"]
  BAT1 = BC9VPC [package=bc9vpc]
  IC1 = IC, DIP package, 8 pins [chip_label="INA126\n"]
  R3 = Trimmer Potentiometer [maximum_resistance=10kΩ package=THT]
  R4 = Resistor [tolerance=±5% resistance=220 package=THT]
  R5 = Resistor [tolerance=±5% resistance=220 package=THT]
  C1 = Ceramic Capacitor [capacitance=100nF package="100 mil [THT, multilayer]"]
  C2 = Ceramic Capacitor [capacitance=100nF package="100 mil [THT, multilayer]"]
  R6 = Trimmer Potentiometer [maximum_resistance=10kΩ package=THT]
  SignOut = female pin header, 2 pins [form="♀ (female)"]

nets (from the schematic view):
  N1: R1.Pin_0, R2.Pin_1, U1.G$1_+IN
  GND: R1.Pin_1, U1.G$1_V-, BAT1.V-, IC1.pin4, C1.0, R6.leg1
  12V: R2.Pin_0, U1.G$1_V+, BAT1.V+, IC1.pin7
  Vcc/2: U1.G$1_OUT, U1.G$1_-IN, IC1.pin5
  N2: U1.G$2_+IN, R5.Pin_1, C1.1
  N3: U1.G$2_-IN, U1.G$2_OUT, C2.1, R6.leg2
  N4: V2-in.pin1, IC1.pin3
  N5: V2-in.pin2, IC1.pin2
  N6: IC1.pin1, R3.wiper
  N7: IC1.pin6, R4.Pin_0
  N8: IC1.pin8, R3.leg1
  N9: R4.Pin_1, R5.Pin_0, C2.0
  N10: R6.wiper, SignOut.pin1
